// Logisim project micron.circ as structural Verilog
module micronme (
  input  Clock,
  input  [2:0] EX,
  input  [5:0] IRQ,
  input  BA,
  input  LOCK,
  input  [3:0] COB,
  input  Reset,
  input  [3:0] COP,
  output [1:0] Status,
  output BE,
  output W,
  output IO,
  output SC,
  output CX,
  output [29:0] Addr,
  output [31:0] Data,
  output [3:0] COE
);

  wire busmaster_avail, cu_busen, cu_busreset, cu_cx, cu_io, cu_sc, cu_w;
  wire [1:0] undriven;
  wire [31:0] busmaster_readout, cu_addr, cu_wdata;

  controlunit cu (
    .IRQ(IRQ), .EX(EX), .RESET(Reset), .COB(COB), .clk(Clock), .RData(busmaster_readout),
    .BusAvail(busmaster_avail), .BusReset(cu_busreset), .WData(cu_wdata), .Addr(cu_addr), .CX(cu_cx),
    .SC(cu_sc), .W(cu_w), .IO(cu_io), .BusEN(cu_busen), .status(Status));  // open: clkout
  busmanager busmaster (
    .SCIn(cu_sc), .WIn(cu_w), .IOIn(cu_io), .BusEN(cu_busen), .Ain(cu_addr), .DIn(cu_wdata), .Clock(Clock),
    .sz(undriven), .Reset(cu_busreset), .LOCK(LOCK), .CXIn(cu_cx), .ACk(BA), .Avail(busmaster_avail),
    .readout(busmaster_readout), .BE(BE), .W(W), .IO(IO), .SC(SC), .AOut(Addr), .DOut(Data), .CX(CX));

  // Notes on the sheet:
  //   COB: pull=down
  //   BA: pull=down
  //   IRQ: pull=down
  //   COP: pull=down
  //   Data: pull=down
  //   EX: pull=down
endmodule

module sysconf (
  input  [4:0] regno,
  output [31:0] Data,
  output [29:0] itaddr
);
endmodule

module busmanager (
  input  SCIn,
  input  WIn,
  input  IOIn,
  input  BusEN,
  input  [31:0] Ain,
  input  [31:0] DIn,
  input  Clock,
  input  [1:0] sz,
  input  Reset,
  input  LOCK,
  input  CXIn,
  input  ACk,
  output Avail,
  output [31:0] readout,
  output BE,
  output W,
  output IO,
  output SC,
  output [29:0] AOut,
  output [31:0] DOut,
  output CX
);

  wire and_2_out, and_3_out, and_4_out, and_5_out, and_6_out, and_7_out, controlled_buffer_1_out,
       counter_1_carry, counter_2_carry, d_ff_1_q, d_ff_2_q, decoder_1_out3, decoder_2_out0, decoder_3_out0,
       extavail_avail, IOBuf_q, multiplexer_1_out, multiplexer_2_out, not_1_out, not_2_out, not_3_out,
       or_1_out, or_3_out, or_4_out, or_5_out, or_6_out, or_7_out, or_8_out, or_9_out, or_10_out, s_r_ff_1_q,
       s_r_ff_1_qn, s_r_ff_2_q, s_r_ff_2_qn, s_r_ff_3_q, SCBuf_q, WBuf_q;
  wire [1:0] ABus_q, counter_1_q, SZBuf_q;
  wire [2:0] counter_2_q;
  wire [29:0] ABuf2_q, ABus_q_2;
  wire [31:0] DBuf2_q, DBus_q, register_2_q;

  and and_1 (Avail, s_r_ff_2_qn, s_r_ff_1_qn);
  S_R_Flip_Flop s_r_ff_1 (
    .S(CXIn), .clk(Clock), .Q(s_r_ff_1_q), .reset(or_5_out), .Qn(s_r_ff_1_qn));  // open: R, preset
  Register #(.width(1)) WBuf (.D(WIn), .en(BusEN), .clk(Clock), .Q(WBuf_q), .clr(or_5_out));
  S_R_Flip_Flop s_r_ff_2 (
    .S(BusEN), .clk(Clock), .Q(s_r_ff_2_q), .reset(or_5_out), .Qn(s_r_ff_2_qn));  // open: R, preset
  and and_2 (and_2_out, BusEN, WIn);
  Register #(.width(1)) SCBuf (.D(SCIn), .en(BusEN), .clk(Clock), .Q(SCBuf_q), .clr(or_5_out));
  Register #(.width(1)) IOBuf (.D(IOIn), .en(BusEN), .clk(Clock), .Q(IOBuf_q), .clr(or_5_out));
  or or_1 (or_1_out, WIn, s_r_ff_1_q);
  or or_2 (s_r_ff_1_q, and_2_out, s_r_ff_1_q);
  Register #(.width(2)) SZBuf (.D(sz), .en(BusEN), .clk(Clock), .Q(SZBuf_q), .clr(or_5_out));
  Register #(.width(32)) ABus (.D(Ain), .en(or_1_out), .clk(Clock), .Q({ABus_q_2, ABus_q}), .clr(or_5_out));
  Register #(.width(32)) DBus (.D(DIn), .en(s_r_ff_1_q), .clk(Clock), .Q(DBus_q), .clr(or_5_out));
  or or_3 (or_3_out, SCBuf_q, s_r_ff_1_q);
  or or_4 (or_4_out, IOBuf_q, s_r_ff_1_q);
  Register #(.width(32)) register_1 (.D(register_2_q), .en(d_ff_1_q), .Q(readout));  // open: clk, clr
  and and_3 (and_3_out, s_r_ff_2_q, extavail_avail);
  or or_5 (or_5_out, counter_1_carry, or_6_out);
  Decoder #(.select(2)) decoder_1 (.out3(decoder_1_out3), .sel(SZBuf_q), .en(s_r_ff_2_q));  // open: out0, out1, out2
  Counter #(.max('h3), .ongoal("stay"), .width(2)) counter_1 (
    .clr(not_1_out), .load(not_1_out), .up(s_r_ff_1_q), .count(s_r_ff_1_q), .clk(Clock),
    .carry(counter_1_carry), .Q(counter_1_q));  // open: D
  not not_1 (not_1_out, s_r_ff_1_q);
  or or_6 (or_6_out, Reset, multiplexer_2_out);
  not not_2 (not_2_out, and_3_out);
  Counter #(.max('h7), .ongoal("stay"), .width(3)) counter_2 (
    .clr(not_2_out), .load(not_2_out), .up(and_3_out), .count(and_3_out), .clk(Clock),
    .carry(counter_2_carry), .Q(counter_2_q));  // open: D
  Decoder #(.select(2)) decoder_2 (
    .out0(decoder_2_out0), .sel(counter_1_q), .en(s_r_ff_1_q));  // open: out1, out2, out3
  and and_4 (and_4_out, ACk, WBuf_q);
  Multiplexer multiplexer_1 (.in0(and_4_out), .in1(WBuf_q), .out(multiplexer_1_out), .sel(decoder_1_out3));
  or or_7 (or_7_out, counter_2_carry, and_5_out);
  buf and_5 (and_5_out, counter_2_q[2]);  // AND_Gate
  Register #(.trigger("falling"), .width(32)) DBuf2 (.D(DBus_q), .en(WBuf_q), .clk(Clock), .Q(DBuf2_q), .clr(or_5_out));
  Multiplexer multiplexer_2 (.in0(or_7_out), .in1(d_ff_2_q), .out(multiplexer_2_out), .sel(multiplexer_1_out));
  Decoder #(.select(2)) decoder_3 (
    .out0(decoder_3_out0), .sel(counter_2_q[1:0]), .en(and_3_out));  // open: out1, out2, out3
  D_Flip_Flop #(.trigger("falling")) d_ff_1 (
    .D(Clock), .clk(Clock), .Q(d_ff_1_q), .reset(or_5_out));  // open: Qn, preset
  D_Flip_Flop #(.trigger("falling")) d_ff_2 (
    .D(d_ff_1_q), .clk(Clock), .Q(d_ff_2_q), .reset(or_5_out));  // open: Qn, preset
  S_R_Flip_Flop s_r_ff_3 (.S(decoder_3_out0), .clk(Clock), .Q(s_r_ff_3_q), .reset(or_5_out));  // open: R, Qn, preset
  S_R_Flip_Flop s_r_ff_4 (.S(decoder_2_out0), .clk(Clock), .Q(CX), .reset(or_5_out));  // open: R, Qn, preset
  busavail extavail (.BE(controlled_buffer_1_out), .Lock(LOCK), .sc(or_3_out), .IO(or_4_out), .AVAIL(extavail_avail));
  assign controlled_buffer_1_out = not_3_out ? BE : 1'bz;  // Controlled_Buffer controlled_buffer_1
  or or_8 (or_8_out, and_7_out, Clock);
  Register #(.trigger("falling"), .width(32)) register_2 (
    .D(DOut), .en(or_9_out), .clk(Clock), .Q(register_2_q), .clr(or_5_out));
  or or_9 (or_9_out, or_8_out, CX);
  not not_3 (not_3_out, s_r_ff_3_q);
  assign BE = s_r_ff_3_q ? s_r_ff_3_q : 1'bz;  // Controlled_Buffer controlled_buffer_2
  Register #(.trigger("falling"), .width(30)) ABuf2 (
    .D(ABus_q_2), .en(or_10_out), .clk(Clock), .Q(ABuf2_q), .clr(or_5_out));
  or or_10 (or_10_out, s_r_ff_3_q, Clock);
  assign W = s_r_ff_3_q ? multiplexer_1_out : 1'bz;  // Controlled_Buffer controlled_buffer_3
  assign SC = s_r_ff_3_q ? or_3_out : 1'bz;  // Controlled_Buffer controlled_buffer_4
  assign AOut = s_r_ff_3_q ? ABuf2_q : 30'bz;  // Controlled_Buffer controlled_buffer_5
  and and_6 (and_6_out, s_r_ff_3_q, multiplexer_1_out);
  assign DOut = and_6_out ? DBuf2_q : 32'bz;  // Controlled_Buffer controlled_buffer_6
  assign W = CX ? CX : 1'bz;  // Controlled_Buffer controlled_buffer_7
  assign IO = CX ? CX : 1'bz;  // Controlled_Buffer controlled_buffer_8
  assign IO = s_r_ff_3_q ? or_4_out : 1'bz;  // Controlled_Buffer controlled_buffer_9
  and and_7 (and_7_out, s_r_ff_3_q, multiplexer_1_out);
  assign SC = CX ? CX : 1'bz;  // Controlled_Buffer controlled_buffer_10
  S_R_Flip_Flop s_r_ff_5 (.S(ACk), .clk(Clock), .Q(Clock), .reset(or_5_out));  // open: R, Qn, preset

  // Notes on the sheet:
  //   IO: pull=down
  //   SC: pull=down
  //   BE: pull=down
  //   W: pull=down
  //   DOut: pull=down
endmodule

module busavail (
  input  BE,
  input  Lock,
  input  sc,
  input  IO,
  output AVAIL
);

  wire or_1_out;

  or or_1 (or_1_out, ~Lock, sc, IO);  // OR_Gate
  and and_1 (AVAIL, ~BE, or_1_out);  // AND_Gate

  // Notes on the sheet:
  //   Lock: pull=down
  //   BE: pull=down
endmodule

module controlunit (
  input  [5:0] IRQ,
  input  [2:0] EX,
  input  RESET,
  input  [3:0] COB,
  input  clk,
  input  [31:0] RData,
  input  BusAvail,
  output BusReset,
  output [31:0] WData,
  output [31:0] Addr,
  output CX,
  output SC,
  output W,
  output IO,
  output BusEN,
  output [1:0] status,
  output clkout
);

  wire statuscu_clocken, undriven, undriven_2, undriven_3;

  and and_1 (clkout, clk, statuscu_clocken);
  statusunit statuscu (
    .COB(COB), .clk(clk), .HLT(undriven_3), .STP(undriven_2), .ISERV(undriven), .RESET(RESET),
    .clocken(statuscu_clocken), .status(status));  // open: COWE
  gprs gprs_1 ();  // open: clock, WData, read0regno, read1regno, wregno, WE, read2regno, Reset, read0data, read1data, read2data
  gprs gprs_2 ();  // open: clock, WData, read0regno, read1regno, wregno, WE, read2regno, Reset, read0data, read1data, read2data

  // Notes on the sheet:
  //   clkout: pull=down
endmodule

module alu (
  input  [31:0] leftin,
  input  [31:0] rightin,
  input  [4:0] shiftq,
  input  shiftp,
  input  [2:0] op,
  output [31:0] result,
  output [3:0] flags
);

  wire adder_1_cout, adder_2_cout, xor_1_out;
  wire [4:0] demultiplexer_1_out0, demultiplexer_1_out1;
  wire [31:0] adder_1_out, adder_2_out, and_1_out, multiplexer_2_out, nor_1_out, not_1_out, or_1_out,
       shifter_1_out, shifter_2_out;

  Demultiplexer #(.width(5)) demultiplexer_1 (
    .out0(demultiplexer_1_out0), .out1(demultiplexer_1_out1), .in(shiftq), .sel(shiftp));
  Shifter #(.width(32)) shifter_1 (.in(leftin), .\dist (demultiplexer_1_out0), .out(shifter_1_out));
  Shifter #(.width(32)) shifter_2 (.in(rightin), .\dist (demultiplexer_1_out1), .out(shifter_2_out));
  assign not_1_out = ~shifter_2_out;  // NOT_Gate not_1, 32 bits wide
  Adder #(.width(32)) adder_1 (
    .a(shifter_1_out), .b(shifter_2_out), .out(adder_1_out), .cin(1'b0), .cout(adder_1_cout));
  Adder #(.width(32)) adder_2 (.a(shifter_1_out), .b(not_1_out), .out(adder_2_out), .cin(1'b1), .cout(adder_2_cout));
  assign and_1_out = shifter_1_out & shifter_2_out;  // AND_Gate and_1, 32 bits wide
  assign or_1_out = shifter_1_out | shifter_2_out;  // OR_Gate or_1, 32 bits wide
  assign nor_1_out = ~(shifter_1_out | shifter_2_out);  // NOR_Gate nor_1, 32 bits wide
  Multiplexer #(.select(3)) multiplexer_1 (
    .in0(1'b0), .in1(adder_1_cout), .in2(adder_2_cout), .in3(1'b0), .in4(1'b0), .in5(1'b0), .in6(1'b0),
    .in7(1'b0), .out(flags[0]), .sel(op));
  Multiplexer #(.select(3), .width(32)) multiplexer_2 (
    .in0(shifter_2_out), .in1(shifter_2_out), .in2(not_1_out), .in3(shifter_2_out), .in4(shifter_2_out),
    .in5(shifter_2_out), .in6(shifter_2_out), .in7(shifter_2_out), .out(multiplexer_2_out), .sel(op));
  xor xor_1 (xor_1_out, leftin[31], multiplexer_2_out[31]);
  Multiplexer #(.select(3), .width(32)) multiplexer_3 (
    .in0(shifter_1_out), .in1(adder_1_out), .in2(adder_2_out), .in3(and_1_out), .in4(or_1_out),
    .in5(nor_1_out), .in6(nor_1_out), .out(result), .sel(op));  // open: in7
  ExactlyOne xor_2 (.out(flags[1]), .in0(flags[2]), .in1(xor_1_out), .in2(flags[0]));
  lflags lflags_1 (.val(result), .zero(flags[3]), .negative(flags[2]));  // open: parity
endmodule

module shiftunit (
  input  [31:0] value,
  input  wrap,
  input  [31:0] shiftq,
  input  dir,
  input  invertsign,
  input  [31:0] remainder,
  output [31:0] result,
  output [3:0] flags
);

  wire and_1_out, and_2_out, or_1_out;
  wire [31:0] bit_extender_1_out, xor_1_out;

  or or_1 (or_1_out, shiftq[5], shiftq[6], shiftq[7], shiftq[8], shiftq[9], shiftq[10], shiftq[11], shiftq[12], shiftq[13], shiftq[14], shiftq[15], shiftq[16], shiftq[17], shiftq[18], shiftq[19], shiftq[20], shiftq[21], shiftq[22], shiftq[23], shiftq[24], shiftq[25], shiftq[26], shiftq[27], shiftq[28], shiftq[29], shiftq[30], shiftq[31]);
  and and_1 (and_1_out, ~wrap, or_1_out);  // AND_Gate
  and and_2 (and_2_out, value[31], invertsign);
  assign bit_extender_1_out = {{31{and_2_out}}, and_2_out};  // Bit_Extender bit_extender_1
  assign xor_1_out = bit_extender_1_out ^ remainder;  // XOR_Gate xor_1, 32 bits wide
  bshifter barrel (
    .val(value), .shiftin(xor_1_out), .dir(dir), .overshift(and_1_out), .shiftq(shiftq[4:0]), .outval(result));  // open: shiftout
  lflags lflags_1 (.val(result), .zero(flags[3]), .negative(flags[2]));  // open: parity

  assign flags[1:0] = 2'b00;
endmodule

module bshifter (
  input  [31:0] val,
  input  [31:0] shiftin,
  input  dir,
  input  overshift,
  input  [4:0] shiftq,
  output [31:0] outval,
  output [31:0] shiftout
);

  wire [1:0] pshift2_1_shiftout;
  wire [3:0] pshift4_1_shiftout;
  wire [7:0] pshift8_1_shiftout;
  wire [15:0] pshift16_1_shiftout;
  wire [30:30] pshift1_1_shiftout;
  wire [31:0] multiplexer_1_out, pshift2_1_nextshift, pshift2_1_outval, pshift4_1_nextshift,
       pshift4_1_outval, pshift8_1_nextshift, pshift8_1_outval, pshift16_1_nextshift, pshift16_1_outval;

  Multiplexer #(.width(32)) multiplexer_1 (.in0(val), .in1(shiftin), .out(multiplexer_1_out), .sel(overshift));
  pshift16 pshift16_1 (
    .base(multiplexer_1_out), .shiftin(shiftin), .dir(dir), .en(shiftq[4]), .outval(pshift16_1_outval),
    .nextshift(pshift16_1_nextshift), .shiftout(pshift16_1_shiftout));
  pshift8 pshift8_1 (
    .base(pshift16_1_outval), .shiftin(pshift16_1_nextshift), .dir(dir), .en(shiftq[3]),
    .outval(pshift8_1_outval), .nextshift(pshift8_1_nextshift), .shiftout(pshift8_1_shiftout));
  pshift4 pshift4_1 (
    .base(pshift8_1_outval), .shiftin(pshift8_1_nextshift), .dir(dir), .en(shiftq[2]),
    .outval(pshift4_1_outval), .nextshift(pshift4_1_nextshift), .shiftout(pshift4_1_shiftout));
  pshift2 pshift2_1 (
    .base(pshift4_1_outval), .shiftin(pshift4_1_nextshift), .dir(shiftq[0]), .en(shiftq[1]),
    .outval(pshift2_1_outval), .nextshift(pshift2_1_nextshift), .shiftout(pshift2_1_shiftout));
  pshift1 pshift1_1 (
    .base(pshift2_1_outval), .shiftin(pshift2_1_nextshift), .dir(dir), .en(shiftq[0]), .outval(outval),
    .shiftout(pshift1_1_shiftout[30]));
  Multiplexer #(.width(32)) multiplexer_2 (
    .in0({1'b0, pshift1_1_shiftout[30], pshift2_1_shiftout, pshift4_1_shiftout, pshift8_1_shiftout, pshift16_1_shiftout}),
    .in1(val), .out(shiftout), .sel(overshift));
endmodule

module pshift16 (
  input  [31:0] base,
  input  [31:0] shiftin,
  input  dir,
  input  en,
  output [31:0] outval,
  output [31:0] nextshift,
  output [15:0] shiftout
);

  wire [15:0] multiplexer_1_out, multiplexer_2_out;

  Multiplexer #(.width(16)) multiplexer_1 (.in0(shiftin[31:16]), .in1(base[31:16]), .out(multiplexer_1_out), .sel(dir));
  Multiplexer #(.width(16)) multiplexer_2 (.in0(base[15:0]), .in1(shiftin[15:0]), .out(multiplexer_2_out), .sel(dir));
  Multiplexer #(.width(16)) multiplexer_3 (.in0(base[15:0]), .in1(multiplexer_1_out), .out(outval[15:0]), .sel(en));
  Multiplexer #(.width(16)) multiplexer_4 (.in0(base[31:16]), .in1(multiplexer_2_out), .out(outval[31:16]), .sel(en));
  Multiplexer #(.width(16)) multiplexer_5 (.in0(shiftin[15:0]), .in1(shiftin[31:16]), .out(nextshift[15:0]), .sel(en));
  Multiplexer #(.width(16)) multiplexer_6 (.in0(shiftin[31:16]), .in1(shiftin[15:0]), .out(nextshift[31:16]), .sel(en));
  Multiplexer #(.enable("true"), .width(16)) multiplexer_7 (
    .in0(base[31:16]), .in1(base[15:0]), .out(shiftout), .sel(dir), .en(en));

  // Notes on the sheet:
  //   Bits 0-15
  //   Bits 16-31
endmodule

module pshift8 (
  input  [31:0] base,
  input  [31:0] shiftin,
  input  dir,
  input  en,
  output [31:0] outval,
  output [31:0] nextshift,
  output [7:0] shiftout
);

  wire [31:0] multiplexer_1_out, multiplexer_2_out;

  Multiplexer #(.width(32)) multiplexer_1 (
    .in0({base[23:0], shiftin[31:24]}), .in1({shiftin[7:0], base[31:8]}), .out(multiplexer_1_out), .sel(dir));
  Multiplexer #(.width(32)) multiplexer_2 (
    .in0({shiftin[23:0], shiftin[31:24]}), .in1({shiftin[7:0], shiftin[31:8]}), .out(multiplexer_2_out),
    .sel(dir));
  Multiplexer #(.enable("true"), .width(8)) multiplexer_3 (
    .in0(shiftin[7:0]), .in1(base[7:0]), .out(shiftout), .sel(dir), .en(en));
  Multiplexer #(.width(32)) multiplexer_4 (.in0(base), .in1(multiplexer_1_out), .out(outval), .sel(en));
  Multiplexer #(.width(32)) multiplexer_5 (.in0(shiftin), .in1(multiplexer_2_out), .out(nextshift), .sel(en));
endmodule

module pshift4 (
  input  [31:0] base,
  input  [31:0] shiftin,
  input  dir,
  input  en,
  output [31:0] outval,
  output [31:0] nextshift,
  output [3:0] shiftout
);

  wire [31:0] multiplexer_1_out, multiplexer_2_out;

  Multiplexer #(.width(32)) multiplexer_1 (
    .in0({base[27:0], shiftin[31:28]}), .in1({shiftin[3:0], base[31:4]}), .out(multiplexer_1_out), .sel(dir));
  Multiplexer #(.width(32)) multiplexer_2 (
    .in0({shiftin[27:0], shiftin[31:28]}), .in1({shiftin[3:0], shiftin[31:4]}), .out(multiplexer_2_out),
    .sel(dir));
  Multiplexer #(.width(32)) multiplexer_3 (.in0(base), .in1(multiplexer_1_out), .out(outval), .sel(en));
  Multiplexer #(.enable("true"), .width(4)) multiplexer_4 (
    .in0(base[31:28]), .in1(base[3:0]), .out(shiftout), .sel(dir), .en(en));
  Multiplexer #(.width(32)) multiplexer_5 (.in0(shiftin), .in1(multiplexer_2_out), .out(nextshift), .sel(en));
endmodule

module pshift2 (
  input  [31:0] base,
  input  [31:0] shiftin,
  input  dir,
  input  en,
  output [31:0] outval,
  output [31:0] nextshift,
  output [1:0] shiftout
);

  wire [31:0] multiplexer_1_out, multiplexer_2_out;

  Multiplexer #(.width(32)) multiplexer_1 (
    .in0({base[29:0], shiftin[31:30]}), .in1({shiftin[1:0], base[31:2]}), .out(multiplexer_1_out), .sel(dir));
  Multiplexer #(.width(32)) multiplexer_2 (
    .in0({shiftin[29:0], shiftin[31:30]}), .in1({shiftin[1:0], shiftin[31:2]}), .out(multiplexer_2_out),
    .sel(dir));
  Multiplexer #(.width(32)) multiplexer_3 (.in0(base), .in1(multiplexer_1_out), .out(outval), .sel(en));
  Multiplexer #(.width(32)) multiplexer_4 (.in0(shiftin), .in1(multiplexer_2_out), .out(nextshift), .sel(en));
  Multiplexer #(.enable("true"), .width(2)) multiplexer_5 (
    .in0(base[31:30]), .in1(base[1:0]), .out(shiftout), .sel(dir), .en(en));
endmodule

module pshift1 (
  input  [31:0] base,
  input  [31:0] shiftin,
  input  dir,
  input  en,
  output [31:0] outval,
  output shiftout
);

  wire [31:0] multiplexer_1_out;

  Multiplexer #(.width(32)) multiplexer_1 (
    .in0({base[30:0], shiftin[31]}), .in1({shiftin[0], base[31:1]}), .out(multiplexer_1_out), .sel(dir));
  Multiplexer #(.enable("true")) multiplexer_2 (.in0(base[31]), .in1(base[0]), .out(shiftout), .sel(dir), .en(en));
  Multiplexer #(.width(32)) multiplexer_3 (.in0(base), .in1(multiplexer_1_out), .out(outval), .sel(en));
endmodule

module lflags (
  input  [31:0] val,
  output parity,
  output zero,
  output negative
);

  xor xor_1 (parity, val[0], val[1], val[2], val[3], val[4], val[5], val[6], val[7], val[8], val[9], val[10], val[11], val[12], val[13], val[14], val[15], val[17], val[18], val[19], val[20], val[21], val[22], val[23], val[24], val[25], val[26], val[27], val[28], val[29], val[30], val[31], val[16]);
  nor nor_1 (zero, val[0], val[1], val[2], val[3], val[4], val[5], val[6], val[7], val[8], val[9], val[10], val[11], val[12], val[13], val[14], val[15], val[17], val[18], val[19], val[20], val[21], val[22], val[23], val[24], val[25], val[26], val[27], val[28], val[29], val[30], val[31], val[16]);

  assign negative = val[31];
endmodule

module instrdecode (
  input  decodeen,
  input  [31:0] iword,
  input  clock,
  output error
);

  wire chk_error, demultiplexer_1_out0, demultiplexer_1_out1, demultiplexer_1_out2, demultiplexer_1_out3,
       demultiplexer_1_out4, demultiplexer_1_out5, demultiplexer_1_out6, demultiplexer_1_out7,
       demultiplexer_1_out8, demultiplexer_1_out9, demultiplexer_1_out10, demultiplexer_1_out11,
       demultiplexer_1_out12, demultiplexer_1_out13, demultiplexer_1_out14, demultiplexer_1_out15,
       demultiplexer_1_out16, demultiplexer_1_out17, demultiplexer_1_out18, demultiplexer_1_out19,
       demultiplexer_1_out20, demultiplexer_1_out21, demultiplexer_1_out22, demultiplexer_1_out23,
       demultiplexer_1_out24, demultiplexer_1_out25, demultiplexer_1_out26, demultiplexer_1_out27,
       demultiplexer_1_out28, demultiplexer_1_out29, demultiplexer_1_out30, demultiplexer_1_out31,
       multiplexer_1_out;
  wire [23:0] decodemasks_data;

  Demultiplexer #(.select(5)) demultiplexer_1 (
    .out0(demultiplexer_1_out0), .out1(demultiplexer_1_out1), .out2(demultiplexer_1_out2),
    .out3(demultiplexer_1_out3), .out4(demultiplexer_1_out4), .out5(demultiplexer_1_out5),
    .out6(demultiplexer_1_out6), .out7(demultiplexer_1_out7), .out8(demultiplexer_1_out8),
    .out9(demultiplexer_1_out9), .out10(demultiplexer_1_out10), .out11(demultiplexer_1_out11),
    .out12(demultiplexer_1_out12), .out13(demultiplexer_1_out13), .out14(demultiplexer_1_out14),
    .out15(demultiplexer_1_out15), .out16(demultiplexer_1_out16), .out17(demultiplexer_1_out17),
    .out18(demultiplexer_1_out18), .out19(demultiplexer_1_out19), .out20(demultiplexer_1_out20),
    .out21(demultiplexer_1_out21), .out22(demultiplexer_1_out22), .out23(demultiplexer_1_out23),
    .out24(demultiplexer_1_out24), .out25(demultiplexer_1_out25), .out26(demultiplexer_1_out26),
    .out27(demultiplexer_1_out27), .out28(demultiplexer_1_out28), .out29(demultiplexer_1_out29),
    .out30(demultiplexer_1_out30), .out31(demultiplexer_1_out31), .in(decodeen), .sel(iword[7:3]));
  Multiplexer #(.enable("true"), .select(5)) multiplexer_1 (
    .in6(1'b1), .in7(1'b1), .in8(1'b1), .in9(1'b1), .in10(1'b1), .in11(1'b1), .in12(1'b1), .in13(1'b1),
    .in14(1'b1), .in15(1'b1), .in16(1'b1), .in17(1'b1), .in18(1'b1), .in19(1'b1), .in20(1'b1), .in21(1'b1),
    .in22(1'b1), .in23(1'b1), .in24(1'b1), .in25(1'b1), .in26(1'b1), .in27(1'b1), .in28(1'b1), .in29(1'b1),
    .in30(1'b1), .in31(1'b1), .out(multiplexer_1_out), .sel(iword[7:3]), .en(decodeen));  // open: in0, in1, in2, in3, in4, in5
  ROM #(.dataWidth(24)) decodemasks (.addr(iword[7:0]), .data(decodemasks_data));
  payloadcheck chk (.payload(iword[31:8]), .mask(decodemasks_data), .error(chk_error));
  or or_1 (error, chk_error, multiplexer_1_out);

  // Notes on the sheet:
  //   contents of decodemasks (hex, n*v repeats v):
  //   0 ffffc0 1c0c00 7ff000 7ff000 0 c0 0 0 5*c00000 20000 20000 0 ffc000 7e000 7e000 0 0 0 ffffe0 ffffe0
  //   23*0 ffffff ffffff
endmodule

module group0decode (
  input  enabled,
  input  [2:0] minor,
  input  clock,
  input  [23:0] payload,
  output error,
  output finished
);

  wire counter_1_carry, decoder_1_out1, decoder_1_out2, not_1_out;

  Decoder #(.select(3)) decoder_1 (
    .out1(decoder_1_out1), .out2(decoder_1_out2), .sel(minor), .en(enabled));  // open: out0, out3, out4, out5, out6, out7
  Counter #(.max('h3f), .ongoal("load"), .width(6)) counter_1 (
    .clr(not_1_out), .load(not_1_out), .up(not_1_out), .count(clock), .clk(clock), .D(payload[5:0]),
    .carry(counter_1_carry));  // open: Q
  not not_1 (not_1_out, decoder_1_out1);
  Multiplexer #(.enable("true"), .select(3)) multiplexer_1 (
    .in0(1'b1), .in1(1'b0), .in2(1'b0), .in3(1'b0), .in4(1'b0), .in5(1'b0), .in6(1'b0), .in7(1'b1),
    .out(error), .sel(minor), .en(enabled));
  Multiplexer #(.enable("true"), .select(3)) multiplexer_2 (
    .in0(1'b0), .in1(counter_1_carry), .out(finished), .sel(minor), .en(enabled));  // open: in2, in3, in4, in5, in6, in7
endmodule

module payloadcheck (
  input  [23:0] payload,
  input  [23:0] mask,
  output error
);

  wire [23:0] and_1_out;

  assign and_1_out = payload & mask;  // AND_Gate and_1, 24 bits wide
  or or_1 (error, and_1_out[0], and_1_out[1], and_1_out[2], and_1_out[3], and_1_out[4], and_1_out[5], and_1_out[6], and_1_out[7], and_1_out[8], and_1_out[9], and_1_out[10], and_1_out[11], and_1_out[13], and_1_out[14], and_1_out[15], and_1_out[16], and_1_out[17], and_1_out[18], and_1_out[19], and_1_out[20], and_1_out[21], and_1_out[22], and_1_out[23], and_1_out[12]);
endmodule

module gprs (
  input  clock,
  input  [31:0] WData,
  input  [4:0] read0regno,
  input  [4:0] read1regno,
  input  [4:0] wregno,
  input  WE,
  input  [4:0] read2regno,
  input  Reset,
  output [31:0] read0data,
  output [31:0] read1data,
  output [31:0] read2data
);

  wire decoder_1_out0, decoder_1_out1, decoder_1_out2, decoder_1_out3;
  wire [31:0] regs0_read1, regs0_read2, regs0_read3, regs0_read4, regs0_read5, regs0_read6, regs0_read7,
       regs1_read0, regs1_read1, regs1_read2, regs1_read3, regs1_read4, regs1_read5, regs1_read6,
       regs1_read7, regs2_read0, regs2_read1, regs2_read2, regs2_read3, regs2_read4, regs2_read5,
       regs2_read6, regs2_read7, regs3_read0, regs3_read1, regs3_read2, regs3_read3, regs3_read4,
       regs3_read5, regs3_read6, regs3_read7;

  Decoder #(.select(2)) decoder_1 (
    .out0(decoder_1_out0), .out1(decoder_1_out1), .out2(decoder_1_out2), .out3(decoder_1_out3),
    .sel(wregno[4:3]), .en(WE));
  regcell8 regs0 (
    .wdata(WData), .clk(clock), .reset(Reset), .regno(wregno[2:0]), .WE(decoder_1_out0), .read1(regs0_read1),
    .read2(regs0_read2), .read3(regs0_read3), .read4(regs0_read4), .read5(regs0_read5), .read6(regs0_read6),
    .read7(regs0_read7));  // open: read0
  regcell8 regs1 (
    .wdata(WData), .clk(clock), .reset(Reset), .regno(wregno[2:0]), .WE(decoder_1_out1), .read0(regs1_read0),
    .read1(regs1_read1), .read2(regs1_read2), .read3(regs1_read3), .read4(regs1_read4), .read5(regs1_read5),
    .read6(regs1_read6), .read7(regs1_read7));
  regcell8 regs2 (
    .wdata(WData), .clk(clock), .reset(Reset), .regno(wregno[2:0]), .WE(decoder_1_out2), .read0(regs2_read0),
    .read1(regs2_read1), .read2(regs2_read2), .read3(regs2_read3), .read4(regs2_read4), .read5(regs2_read5),
    .read6(regs2_read6), .read7(regs2_read7));
  regcell8 regs3 (
    .wdata(WData), .clk(clock), .reset(Reset), .regno(wregno[2:0]), .WE(decoder_1_out3), .read0(regs3_read0),
    .read1(regs3_read1), .read2(regs3_read2), .read3(regs3_read3), .read4(regs3_read4), .read5(regs3_read5),
    .read6(regs3_read6), .read7(regs3_read7));
  Multiplexer #(.select(5), .width(32)) multiplexer_1 (
    .in0({32{1'b0}}), .in1(regs0_read1), .in2(regs0_read2), .in3(regs0_read3), .in4(regs0_read4),
    .in5(regs0_read5), .in6(regs0_read6), .in7(regs0_read7), .in8(regs1_read0), .in9(regs1_read1),
    .in10(regs1_read2), .in11(regs1_read3), .in12(regs1_read4), .in13(regs1_read5), .in14(regs1_read6),
    .in15(regs1_read7), .in16(regs2_read0), .in17(regs2_read1), .in18(regs2_read2), .in19(regs2_read3),
    .in20(regs2_read4), .in21(regs2_read5), .in22(regs2_read6), .in23(regs2_read7), .in24(regs3_read0),
    .in25(regs3_read1), .in26(regs3_read2), .in27(regs3_read3), .in28(regs3_read4), .in29(regs3_read5),
    .in30(regs3_read6), .in31(regs3_read7), .out(read0data), .sel(read0regno));
  Multiplexer #(.select(5), .width(32)) multiplexer_2 (
    .in0({32{1'b0}}), .in1(regs0_read1), .in2(regs0_read2), .in3(regs0_read3), .in4(regs0_read4),
    .in5(regs0_read5), .in6(regs0_read6), .in7(regs0_read7), .in8(regs1_read0), .in9(regs1_read1),
    .in10(regs1_read2), .in11(regs1_read3), .in12(regs1_read4), .in13(regs1_read5), .in14(regs1_read6),
    .in15(regs1_read7), .in16(regs2_read0), .in17(regs2_read1), .in18(regs2_read2), .in19(regs2_read3),
    .in20(regs2_read4), .in21(regs2_read5), .in22(regs2_read6), .in23(regs2_read7), .in24(regs3_read0),
    .in25(regs3_read1), .in26(regs3_read2), .in27(regs3_read3), .in28(regs3_read4), .in29(regs3_read5),
    .in30(regs3_read6), .in31(regs3_read7), .out(read2data), .sel(read2regno));
  Multiplexer #(.select(5), .width(32)) multiplexer_3 (
    .in0({32{1'b0}}), .in1(regs0_read1), .in2(regs0_read2), .in3(regs0_read3), .in4(regs0_read4),
    .in5(regs0_read5), .in6(regs0_read6), .in7(regs0_read7), .in8(regs1_read0), .in9(regs1_read1),
    .in10(regs1_read2), .in11(regs1_read3), .in12(regs1_read4), .in13(regs1_read5), .in14(regs1_read6),
    .in15(regs1_read7), .in16(regs2_read0), .in17(regs2_read1), .in18(regs2_read2), .in19(regs2_read3),
    .in20(regs2_read4), .in21(regs2_read5), .in22(regs2_read6), .in23(regs2_read7), .in24(regs3_read0),
    .in25(regs3_read1), .in26(regs3_read2), .in27(regs3_read3), .in28(regs3_read4), .in29(regs3_read5),
    .in30(regs3_read6), .in31(regs3_read7), .out(read1data), .sel(read1regno));
endmodule

module statusunit (
  input  [3:0] COWE,
  input  [3:0] COB,
  input  clk,
  input  HLT,
  input  STP,
  input  ISERV,
  input  RESET,
  output clocken,
  output [1:0] status
);

  wire or_1_out, s_r_ff_1_q, s_r_ff_2_q, s_r_ff_3_q, s_r_ff_4_q, s_r_ff_5_q, s_r_ff_6_q;
  wire [3:0] not_1_out;

  assign not_1_out = ~COB;  // NOT_Gate not_1, 4 bits wide
  S_R_Flip_Flop s_r_ff_1 (.S(COWE[0]), .R(clk), .clk(clk), .Q(s_r_ff_1_q), .reset(not_1_out[0]));  // open: Qn, preset
  S_R_Flip_Flop s_r_ff_2 (.S(HLT), .R(clk), .clk(clk), .Q(s_r_ff_2_q), .reset(clk));  // open: Qn, preset
  S_R_Flip_Flop s_r_ff_3 (.S(STP), .R(clk), .clk(clk), .Q(s_r_ff_3_q));  // open: reset, Qn, preset
  S_R_Flip_Flop s_r_ff_4 (.S(COWE[3]), .R(clk), .clk(clk), .Q(s_r_ff_4_q), .reset(not_1_out[3]));  // open: Qn, preset
  S_R_Flip_Flop s_r_ff_5 (.S(COWE[1]), .R(clk), .clk(clk), .Q(s_r_ff_5_q), .reset(not_1_out[1]));  // open: Qn, preset
  S_R_Flip_Flop s_r_ff_6 (.S(COWE[2]), .R(clk), .clk(clk), .Q(s_r_ff_6_q), .reset(not_1_out[2]));  // open: Qn, preset
  or or_1 (or_1_out, s_r_ff_1_q, s_r_ff_5_q, s_r_ff_6_q, s_r_ff_4_q);
  Priority_Encoder #(.select(2)) priority_encoder_1 (
    .in0(1'b1), .in1(or_1_out), .in2(s_r_ff_2_q), .in3(s_r_ff_3_q), .out(status), .en_in(1'b1));  // open: gs, en_out
  or or_2 (clocken, or_1_out, s_r_ff_2_q, s_r_ff_3_q);

  assign ISERV = clk;
  assign RESET = clk;
endmodule

module ioregs (
  input  [31:0] readval,
  input  clock,
  input  reset,
  input  [4:0] readreg,
  input  [4:0] wregno,
  input  WE,
  input  SE,
  input  [31:0] writeval,
  input  [4:0] width,
  input  [31:0] portout
);

  wire demultiplexer_1_out0, demultiplexer_1_out1, demultiplexer_1_out2, demultiplexer_1_out3, nor_1_out,
       or_1_out;
  wire [4:0] negator_1_out;
  wire [31:0] bshifter_1_outval, bshifter_1_shiftout, io0_read0, io0_read1, io0_read2, io0_read3, io0_read4,
       io0_read5, io0_read6, io0_read7, io1_read0, io1_read1, io1_read2, io1_read3, io1_read4, io1_read5,
       io1_read6, io1_read7, io2_read0, io2_read1, io2_read2, io2_read3, io2_read4, io2_read5, io2_read6,
       io2_read7, io3_read0, io3_read1, io3_read2, io3_read3, io3_read4, io3_read5, io3_read6, io3_read7,
       multiplexer_1_out, multiplexer_2_out;

  Demultiplexer #(.select(2)) demultiplexer_1 (
    .out0(demultiplexer_1_out0), .out1(demultiplexer_1_out1), .out2(demultiplexer_1_out2),
    .out3(demultiplexer_1_out3), .in(or_1_out), .sel(wregno[4:3]));
  or or_1 (or_1_out, WE, SE);
  nor nor_1 (nor_1_out, width[0], width[1], width[2], width[3], width[4]);
  regcell8 io0 (
    .wdata(multiplexer_1_out), .clk(clock), .reset(reset), .regno(wregno[2:0]), .WE(demultiplexer_1_out0),
    .read0(io0_read0), .read1(io0_read1), .read2(io0_read2), .read3(io0_read3), .read4(io0_read4),
    .read5(io0_read5), .read6(io0_read6), .read7(io0_read7));
  regcell8 io1 (
    .wdata(multiplexer_1_out), .clk(clock), .reset(reset), .regno(wregno[2:0]), .WE(demultiplexer_1_out1),
    .read0(io1_read0), .read1(io1_read1), .read2(io1_read2), .read3(io1_read3), .read4(io1_read4),
    .read5(io1_read5), .read6(io1_read6), .read7(io1_read7));
  Multiplexer #(.width(32)) multiplexer_1 (.in0(writeval), .in1(bshifter_1_outval), .out(multiplexer_1_out), .sel(SE));
  Multiplexer #(.enable("true"), .select(5), .width(32)) multiplexer_2 (
    .in0(io0_read0), .in1(io0_read1), .in2(io0_read2), .in3(io0_read3), .in4(io0_read4), .in5(io0_read5),
    .in6(io0_read6), .in7(io0_read7), .in8(io1_read0), .in9(io1_read1), .in10(io1_read2), .in11(io1_read3),
    .in12(io1_read4), .in13(io1_read5), .in14(io1_read6), .in15(io1_read7), .in16(io2_read0),
    .in17(io2_read1), .in18(io2_read2), .in19(io2_read3), .in20(io2_read4), .in21(io2_read5),
    .in22(io2_read6), .in23(io2_read7), .in24(io3_read0), .in25(io3_read1), .in26(io3_read2),
    .in27(io3_read3), .in28(io3_read4), .in29(io3_read5), .in30(io3_read6), .in31(io3_read7),
    .out(multiplexer_2_out), .en(SE));  // open: sel
  bshifter bshifter_1 (
    .val(multiplexer_2_out), .shiftin(writeval), .dir(1'b1), .overshift(nor_1_out), .shiftq(width),
    .outval(bshifter_1_outval), .shiftout(bshifter_1_shiftout));
  regcell8 io2 (
    .wdata(multiplexer_1_out), .clk(clock), .reset(reset), .regno(wregno[2:0]), .WE(demultiplexer_1_out2),
    .read0(io2_read0), .read1(io2_read1), .read2(io2_read2), .read3(io2_read3), .read4(io2_read4),
    .read5(io2_read5), .read6(io2_read6), .read7(io2_read7));
  regcell8 io3 (
    .wdata(multiplexer_1_out), .clk(clock), .reset(reset), .regno(wregno[2:0]), .WE(demultiplexer_1_out3),
    .read0(io3_read0), .read1(io3_read1), .read2(io3_read2), .read3(io3_read3), .read4(io3_read4),
    .read5(io3_read5), .read6(io3_read6), .read7(io3_read7));
  Negator #(.width(5)) negator_1 (.in(width), .out(negator_1_out));
  Shifter #(.shift("lr"), .width(32)) shifter_1 (.in(bshifter_1_shiftout), .\dist (negator_1_out), .out(portout));
  Multiplexer #(.select(5), .width(32)) multiplexer_3 (
    .in0(io0_read0), .in1(io0_read1), .in2(io0_read2), .in3(io0_read3), .in4(io0_read4), .in5(io0_read5),
    .in6(io0_read6), .in7(io0_read7), .in8(io1_read0), .in9(io1_read1), .in10(io1_read2), .in11(io1_read3),
    .in12(io1_read4), .in13(io1_read5), .in14(io1_read6), .in15(io1_read7), .in16(io2_read0),
    .in17(io2_read1), .in18(io2_read2), .in19(io2_read3), .in20(io2_read4), .in21(io2_read5),
    .in22(io2_read6), .in23(io2_read7), .in24(io3_read0), .in25(io3_read1), .in26(io3_read2),
    .in27(io3_read3), .in28(io3_read4), .in29(io3_read5), .in30(io3_read6), .in31(io3_read7), .out(readval),
    .sel(readreg));
endmodule

module regcell8 (
  input  [31:0] wdata,
  input  clk,
  input  reset,
  input  [2:0] regno,
  input  WE,
  output [31:0] read0,
  output [31:0] read1,
  output [31:0] read2,
  output [31:0] read3,
  output [31:0] read4,
  output [31:0] read5,
  output [31:0] read6,
  output [31:0] read7
);

  wire decoder_1_out0, decoder_1_out1, decoder_1_out2, decoder_1_out3, decoder_1_out4, decoder_1_out5,
       decoder_1_out6, decoder_1_out7;

  Register #(.trigger("falling"), .width(32)) register_1 (
    .D(wdata), .en(decoder_1_out0), .clk(clk), .Q(read0), .clr(reset));
  Register #(.trigger("falling"), .width(32)) register_2 (
    .D(wdata), .en(decoder_1_out1), .clk(clk), .Q(read1), .clr(reset));
  Register #(.trigger("falling"), .width(32)) register_3 (
    .D(wdata), .en(decoder_1_out2), .clk(clk), .Q(read2), .clr(reset));
  Register #(.trigger("falling"), .width(32)) register_4 (
    .D(wdata), .en(decoder_1_out3), .clk(clk), .Q(read3), .clr(reset));
  Decoder #(.select(3)) decoder_1 (
    .out0(decoder_1_out0), .out1(decoder_1_out1), .out2(decoder_1_out2), .out3(decoder_1_out3),
    .out4(decoder_1_out4), .out5(decoder_1_out5), .out6(decoder_1_out6), .out7(decoder_1_out7), .sel(regno),
    .en(WE));
  Register #(.trigger("falling"), .width(32)) register_5 (
    .D(wdata), .en(decoder_1_out4), .clk(clk), .Q(read4), .clr(reset));
  Register #(.trigger("falling"), .width(32)) register_6 (
    .D(wdata), .en(decoder_1_out5), .clk(clk), .Q(read5), .clr(reset));
  Register #(.trigger("falling"), .width(32)) register_7 (
    .D(wdata), .en(decoder_1_out6), .clk(clk), .Q(read6), .clr(reset));
  Register #(.trigger("falling"), .width(32)) register_8 (
    .D(wdata), .en(decoder_1_out7), .clk(clk), .Q(read7), .clr(reset));
endmodule
